# Fritzing sketch 3_in_1_robot (saved by Fritzing 0.9.9b)
circuit board: 10.255cm x 13.0675cm
breadboards: 1

parts:
  Left-Front = gear-motor
  Right-Front = gear-motor
  Right-Back = gear-motor
  Arduino_Nano = Arduino Nano (Rev3.0)
  HC-SR04 = HC-SR04 Ultrasonic Distance Sensor
  IR-receiver = KY-022 Infrared Receiver Module [package="Breakout board"]
  DGServo_9g = Dagu DGServo 9g (Top view) [part_number=RS001B]
  L298N = L298N DC motor driver
  Left-Back = gear-motor
  VCC1 = Battery
  Part1 = Bluetooth HC-06 Macho

nets:
  N1: Left-Front.pin_1, L298N.OUT4, Left-Back.pin_2
  N2: Left-Front.pin_2, L298N.OUT3, Left-Back.pin_1
  N3: Right-Front.pin_1, Right-Back.pin_2, L298N.OUT1
  N4: Right-Front.pin_2, Right-Back.pin_1, L298N.OUT2
  N5: Arduino_Nano.D1/TX, Part1.RXD
  N6: Arduino_Nano.D0/RX, Part1.TXD
  GND: Arduino_Nano.GND, HC-SR04.GND, IR-receiver.-, DGServo_9g.gnd, L298N.GND, VCC1.-, Part1.GND
  N7: Arduino_Nano.D2, HC-SR04.ECHO
  N8: Arduino_Nano.D3, HC-SR04.TRIG
  N9: Arduino_Nano.D4, L298N.IN4
  N10: Arduino_Nano.D5, L298N.IN3
  N11: Arduino_Nano.D6, L298N.IN2
  N12: Arduino_Nano.D7, L298N.IN1
  N13: Arduino_Nano.D8, IR-receiver.S
  N14: Arduino_Nano.D9, DGServo_9g.pulse
  VIN: Arduino_Nano.VIN, L298N.12V, VCC1.+
  VCC: Arduino_Nano.5V, HC-SR04.VCC, IR-receiver.Vin, DGServo_9g.vcc, Part1.VCC

custom parts:
  KY-022 Infrared Receiver Module: KY-022 IR receiver module, reacts to 38kHz infrared light.
  L298N DC motor driver: 2x DC motor driver with 78M05 positive voltage regulator (7..35 V) L298N: max 46 V, 2 A Set 5 V Enable jumper to enable 5 V regultor (needed for the L298N) and +5 V output at screw terminal or supply external +5 V at screw terminal Set ENA and/or ENB to +5 V to enable motor permanently or supply ENA and/or ENB with PWM signal IN1 and IN2 set rotation directory for motor A (OUT1/OUT2) IN2 and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
  Battery: Your standard 2x 18650 battery pack (7.4 Volts)

// code stored in the sketch: 3_in_1_robot.ino
#include <Servo.h>
#include <NewPing.h>  			// Ultrasonic sensor
#include <IRremote.h> 
#include <SoftwareSerial.h> // Bluetooth communication

// Directions
#define STRAIGHT 100
#define LEFT     180
#define RIGHT    10
// IRremote's buttons
#define ON    0xFFA25D
#define OFF   0xFFE21D
#define MODE1 0xFFE01F
#define MODE2 0xFFA857
#define MODE3 0xFF906F
#define SOS   0xFF18E7
#define HOLD  0xFFFFFFFF
// Pins
#define RX   0
#define TX   1
#define ECHO 2
#define TRIG 3

SoftwareSerial BTserial(RX, TX); 

NewPing sonar(TRIG, ECHO, 250);

Servo servo;

IRrecv irrecv(9);
decode_results button;

const int motors[] = {7,6,5,4}; //L298N pins
int distance = 100, mode = 0;
char last_command;

void setup() {
  for(int i : motors) pinMode(i, OUTPUT);
  servo.attach(8);
  servo.write(STRAIGHT);
  irrecv.enableIRIn();
  Serial.begin(9600);
}

void loop() {
	if(mode != 3 && irrecv.decode(&button)){
    switchMode(button.value);
    irrecv.resume();
  }
  if(mode != 2 && Serial.available()){		
		switchMode(Serial.read());    
  }
  switch(mode){
  case 0: // Stanby mode
    stop();
    servo.write(STRAIGHT);
    break;
  case 1: obstacleAvoiding();			break;
  case 2: bluetoothControlling();	break;		
  case 3: irControlling();				break;
	}
}

void switchMode(int data){
  switch(data){
  case ON:
    if(mode == 0)
      mode = 1;
    break;
  case OFF: case '4':
		mode = 0;
    break;
  case MODE1: case '1':
    mode = 1; 
    break;
  case MODE2: case '2':
    mode = 2;
		Serial.read();
    break;
  case MODE3: case '3':
    mode = 3;
    break;    
  } 
}

void obstacleAvoiding(){
	if(distance < 30){
		stop();
		delay(300);
		moveBackward();
		delay(400);
		stop();
		delay(300);
		getDistance(LEFT) > getDistance(RIGHT) ? turnLeft() : turnRight();
		delay(400);
		stop();
	}
	else moveForward(); 
	distance = getDistance(STRAIGHT);
}

int getDistance(int DIRECTION){
  servo.write(DIRECTION);
  delay(70);
  int newDistance = sonar.ping_cm();
  if(DIRECTION != STRAIGHT){
    delay(500);
    servo.write(STRAIGHT);
  }
  return newDistance == 0 ? 250 : newDistance;  
}

void bluetoothControlling(){
	if(Serial.available()){
		switch(Serial.read()){
		case '1':
			switchMode(OFF);
			Serial.read();
			break;
		case '2': servo.write(RIGHT);     break;      
		case '3': servo.write(STRAIGHT);  break;
		case '4': servo.write(LEFT);		 	break;
		case 'N': moveForward();          break;
		case 'S': moveBackward();         break;
		case 'W': turnLeft();             break;
		case 'E': turnRight();            break;
		}
	}
	delay(60);
	stop();
}

void irControlling(){
	if(irrecv.decode(&button)){			
		translateIR(button.value);
		irrecv.resume();
	}
	delay(200); 
	stop();
}

void translateIR(int data){
	switch(data){
	case OFF:
		switchMode(OFF);
		break;
	case MODE1: case 'L':
		turnLeft();
		last_command = 'L';
		break;
	case MODE2: case 'F':
		moveForward();
		last_command = 'F';
		break;			 
	case MODE3: case 'R':
		turnRight();
		last_command = 'R';
		break;					
	case SOS: case 'B':
		moveBackward();
		last_command = 'B';
		break;
	case HOLD:
		translateIR(last_command);
		break;
	}
}

void stop(){
  for(int i : motors){
    digitalWrite(i, LOW);
  }
}

void moveForward(){
  digitalWrite(motors[0], HIGH); //IN1
  digitalWrite(motors[1], LOW);  //IN2
  digitalWrite(motors[2], HIGH); //IN3
  digitalWrite(motors[3], LOW);  //IN4
}

void moveBackward(){
  digitalWrite(motors[0], LOW);
  digitalWrite(motors[1], HIGH);
  digitalWrite(motors[2], LOW);
  digitalWrite(motors[3], HIGH);
}

void turnLeft(){
  digitalWrite(motors[0], HIGH);
  digitalWrite(motors[1], LOW);
  digitalWrite(motors[2], LOW);
  digitalWrite(motors[3], HIGH); 
}

void turnRight(){
	digitalWrite(motors[0], LOW);
	digitalWrite(motors[1], HIGH);
	digitalWrite(motors[2], HIGH);
	digitalWrite(motors[3], LOW);  
}
